// Digital circuit fd.dig as structural Verilog
module fd (
  input  [7:0] A,
  input  [7:0] B,
  input  clock,
  input  [1:0] sela,
  input  selb,
  input  cear,
  input  cebr,
  output [7:0] mdc,
  output igual,
  output menor
);

  wire [7:0] B_q, multiplexer_1_out, multiplexer_2_out, sub_1_s;

  Multiplexer #(.Bits(8), .Selector_Bits(2)) multiplexer_1 (
    .sel(sela), .in_0(A), .in_1(sub_1_s), .in_2(B_q), .in_3({8{1'b0}}), .out(multiplexer_1_out));
  Multiplexer #(.Bits(8)) multiplexer_2 (.sel(selb), .in_0(B), .in_1(A), .out(multiplexer_2_out));
  Register #(.Bits(8)) u_A (.D(multiplexer_1_out), .C(clock), .en(cear), .Q(mdc));
  Register #(.Bits(8)) u_B (.D(multiplexer_2_out), .C(clock), .en(cebr), .Q(B_q));
  Sub #(.Bits(8)) sub_1 (.a(mdc), .b(B_q), .c_i(1'b0), .s(sub_1_s));  // open: c_o
  Comparator #(.Bits(8)) comparator_1 (.a(mdc), .b(B_q), .eq(igual), .lt(menor));  // open: gt
endmodule
